// Logisim project project 2.circ as structural Verilog: 1 circuit, main circuit solution
module solution (
  input  [5:0] A,
  input  [5:0] B,
  output [5:0] R
);

  wire [5:0] adder_1_out, and_1_out, and_2_out, not_1_out, not_2_out, subtractor_1_out;
  wire [5:5] subtractor_1_bout;

  // Probe on A
  // Probe on B
  Subtractor #(.width(6)) subtractor_1 (
    .a(A), .b(B), .out(subtractor_1_out), .bout(subtractor_1_bout[5]));  // open: bin
  assign not_1_out = ~subtractor_1_out;  // NOT_Gate not_1, 6 bits wide
  Adder #(.width(6)) adder_1 (.a(not_1_out), .b(6'b000001), .out(adder_1_out));  // open: cin, cout
  assign and_1_out = subtractor_1_out & not_2_out;  // AND_Gate and_1, 6 bits wide
  assign not_2_out = ~{6{subtractor_1_bout[5]}};  // NOT_Gate not_2, 6 bits wide
  assign and_2_out = {6{subtractor_1_bout[5]}} & adder_1_out;  // AND_Gate and_2, 6 bits wide
  // Probe on R
  assign R = and_1_out | and_2_out;  // OR_Gate or_1, 6 bits wide
endmodule
